// Logisim project 4addhalf.circ as structural Verilog: 1 circuit, main circuit main
module main (
  input  [1:0] Sum,
  input  [1:0] A,
  input  [1:0] B,
  output carry
);

  wire and_1_out, nand_1_out, nand_2_out, nand_3_out, xor_2_out;

  xor xor_1 (Sum[0], A[0], B[0]);
  and and_1 (and_1_out, A[0], B[0]);
  xor xor_2 (xor_2_out, A[1], B[1]);
  xor xor_3 (Sum[1], and_1_out, xor_2_out);
  nand nand_1 (nand_1_out, and_1_out, B[0]);
  nand nand_2 (nand_2_out, and_1_out, A[0]);
  nand nand_3 (nand_3_out, B[0], A[0]);
  nand nand_4 (carry, nand_1_out, nand_2_out, nand_3_out);
endmodule
