// Logisim project 7tube.circ as structural Verilog: 1 circuit, main circuit main
module main (
  input  A,
  input  B,
  input  C,
  input  D,
  output P6,
  output P5,
  output P4,
  output P3,
  output P2,
  output P1,
  output P0
);

  wire and_1_out, and_2_out, and_3_out, and_4_out, and_5_out, and_6_out, and_7_out, and_8_out, and_9_out,
       and_10_out, and_11_out, and_12_out, and_13_out, and_14_out, and_15_out, and_16_out, and_17_out,
       and_18_out, and_19_out, and_20_out, and_21_out, and_22_out, and_23_out, and_24_out, and_25_out,
       and_26_out, and_27_out, and_28_out, and_29_out, and_30_out, and_31_out, and_32_out, and_33_out,
       and_34_out, and_35_out, and_36_out, and_37_out, and_38_out, and_39_out, and_40_out, and_41_out,
       and_42_out, and_43_out, and_44_out, and_45_out, and_46_out, and_47_out, and_48_out, and_49_out,
       and_50_out, and_51_out, and_52_out, and_53_out, not_1_out, not_2_out, not_3_out, not_4_out, not_5_out,
       not_6_out, not_7_out, not_8_out, not_9_out, not_10_out, not_11_out, not_12_out, not_13_out,
       not_14_out, not_15_out, not_16_out, not_17_out, not_18_out, not_19_out, not_20_out, not_21_out,
       not_22_out, not_23_out, not_24_out, not_25_out, not_26_out, not_27_out, not_28_out, not_29_out,
       not_30_out, not_31_out, not_32_out, not_33_out, not_34_out, not_35_out, not_36_out, not_37_out,
       not_38_out, not_39_out, not_40_out, not_41_out, not_42_out, not_43_out, not_44_out, not_45_out,
       not_46_out, not_47_out, not_48_out, not_49_out, or_1_out, or_2_out, or_3_out, or_4_out, or_5_out,
       or_6_out, or_7_out, or_8_out, or_9_out, or_10_out, or_11_out, or_12_out, or_13_out, or_14_out,
       or_15_out, or_16_out, or_17_out, or_18_out, or_19_out, or_20_out, or_21_out, or_23_out, or_24_out;

  not not_1 (not_1_out, B);
  not not_2 (not_2_out, D);
  not not_3 (not_3_out, A);
  not not_4 (not_4_out, A);
  and and_1 (and_1_out, A, not_5_out);
  not not_5 (not_5_out, B);
  not not_6 (not_6_out, C);
  not not_7 (not_7_out, C);
  not not_8 (not_8_out, D);
  not not_9 (not_9_out, A);
  and and_2 (and_2_out, not_9_out, B);
  not not_10 (not_10_out, C);
  not not_11 (not_11_out, A);
  and and_3 (and_3_out, not_11_out, not_12_out);
  not not_12 (not_12_out, B);
  not not_13 (not_13_out, D);
  not not_14 (not_14_out, B);
  and and_4 (and_4_out, not_14_out, not_15_out);
  not not_15 (not_15_out, C);
  not not_16 (not_16_out, D);
  not not_17 (not_17_out, A);
  not not_18 (not_18_out, A);
  and and_5 (and_5_out, not_18_out, not_19_out);
  not not_19 (not_19_out, B);
  not not_20 (not_20_out, D);
  not not_21 (not_21_out, B);
  and and_6 (and_6_out, not_21_out, C);
  not not_22 (not_22_out, C);
  not not_23 (not_23_out, A);
  and and_7 (and_7_out, not_23_out, not_24_out);
  not not_24 (not_24_out, C);
  not not_25 (not_25_out, A);
  and and_8 (and_8_out, not_25_out, D);
  not not_26 (not_26_out, C);
  not not_27 (not_27_out, A);
  not not_28 (not_28_out, B);
  not not_29 (not_29_out, A);
  not not_30 (not_30_out, B);
  not not_31 (not_31_out, A);
  and and_9 (and_9_out, not_31_out, not_32_out);
  not not_32 (not_32_out, C);
  not not_33 (not_33_out, D);
  not not_34 (not_34_out, A);
  and and_10 (and_10_out, not_34_out, C);
  and and_11 (and_11_out, A, not_35_out);
  not not_35 (not_35_out, C);
  not not_36 (not_36_out, B);
  and and_12 (and_12_out, not_36_out, C);
  and and_13 (and_13_out, C, not_37_out);
  not not_37 (not_37_out, D);
  not not_38 (not_38_out, A);
  and and_14 (and_14_out, not_38_out, B);
  not not_39 (not_39_out, C);
  not not_40 (not_40_out, B);
  and and_15 (and_15_out, not_1_out, not_2_out);
  and and_16 (and_16_out, not_3_out, C);
  and and_17 (and_17_out, not_4_out, B);
  and and_18 (and_18_out, B, C);
  and and_19 (and_19_out, and_1_out, not_6_out);
  not not_41 (not_41_out, D);
  and and_20 (and_20_out, not_7_out, not_8_out);
  and and_21 (and_21_out, and_2_out, not_10_out);
  not not_42 (not_42_out, D);
  not not_43 (not_43_out, B);
  and and_22 (and_22_out, and_3_out, not_13_out);
  and and_23 (and_23_out, and_4_out, not_16_out);
  and and_24 (and_24_out, not_17_out, C);
  not not_44 (not_44_out, D);
  and and_25 (and_25_out, A, C);
  and and_26 (and_26_out, and_5_out, not_20_out);
  and and_27 (and_27_out, and_6_out, D);
  and and_28 (and_28_out, B, not_22_out);
  and and_29 (and_29_out, B, C);
  not not_45 (not_45_out, D);
  not not_46 (not_46_out, C);
  or or_1 (or_1_out, and_7_out, and_8_out);
  and and_30 (and_30_out, not_26_out, D);
  and and_31 (and_31_out, not_27_out, B);
  and and_32 (and_32_out, A, not_28_out);
  and and_33 (and_33_out, not_29_out, not_30_out);
  and and_34 (and_34_out, and_9_out, not_33_out);
  not not_47 (not_47_out, B);
  not not_48 (not_48_out, C);
  and and_35 (and_35_out, and_10_out, D);
  and and_36 (and_36_out, and_11_out, D);
  and and_37 (and_37_out, A, C);
  not not_49 (not_49_out, D);
  or or_2 (or_2_out, and_12_out, and_13_out);
  and and_38 (and_38_out, and_14_out, not_39_out);
  and and_39 (and_39_out, A, not_40_out);
  and and_40 (and_40_out, A, D);
  or or_3 (or_3_out, and_15_out, and_16_out);
  and and_41 (and_41_out, and_17_out, D);
  or or_4 (or_4_out, and_18_out, and_19_out);
  and and_42 (and_42_out, A, not_41_out);
  or or_5 (or_5_out, and_20_out, and_21_out);
  and and_43 (and_43_out, B, not_42_out);
  and and_44 (and_44_out, A, not_43_out);
  and and_45 (and_45_out, A, C);
  or or_6 (or_6_out, and_22_out, and_23_out);
  and and_46 (and_46_out, and_24_out, not_44_out);
  and and_47 (and_47_out, and_25_out, D);
  and and_48 (and_48_out, A, B);
  or or_7 (or_7_out, and_26_out, and_27_out);
  and and_49 (and_49_out, and_28_out, D);
  and and_50 (and_50_out, and_29_out, not_45_out);
  and and_51 (and_51_out, A, not_46_out);
  or or_8 (or_8_out, or_1_out, and_30_out);
  or or_9 (or_9_out, and_31_out, and_32_out);
  or or_10 (or_10_out, and_33_out, and_34_out);
  and and_52 (and_52_out, not_47_out, not_48_out);
  or or_11 (or_11_out, and_35_out, and_36_out);
  and and_53 (and_53_out, and_37_out, not_49_out);
  or or_12 (or_12_out, or_2_out, and_38_out);
  or or_13 (or_13_out, and_39_out, and_40_out);
  or or_14 (or_14_out, or_3_out, and_41_out);
  or or_15 (or_15_out, or_4_out, and_42_out);
  or or_16 (or_16_out, or_5_out, and_43_out);
  or or_17 (or_17_out, and_44_out, and_45_out);
  or or_18 (or_18_out, or_6_out, and_46_out);
  or or_19 (or_19_out, and_47_out, and_48_out);
  or or_20 (or_20_out, or_7_out, and_49_out);
  or or_21 (or_21_out, and_50_out, and_51_out);
  or or_22 (P2, or_8_out, or_9_out);
  or or_23 (or_23_out, or_10_out, and_52_out);
  or or_24 (or_24_out, or_11_out, and_53_out);
  or or_25 (P0, or_12_out, or_13_out);
  or or_26 (P6, or_14_out, or_15_out);
  or or_27 (P5, or_16_out, or_17_out);
  or or_28 (P4, or_18_out, or_19_out);
  or or_29 (P3, or_20_out, or_21_out);
  or or_30 (P1, or_23_out, or_24_out);
endmodule
