// Logisim project CRC.circ as structural Verilog: 2 circuits, main circuit mod2div
module mod2div (
  input  [3:0] divisor,
  input  [3:0] dividend,
  output [2:0] remainder
);

  wire not_1_out;
  wire [3:0] controlled_buffer_1_out, xor_1_out;

  assign controlled_buffer_1_out = not_1_out ? dividend : 4'bz;  // Controlled_Buffer controlled_buffer_1
  not not_1 (not_1_out, dividend[3]);
  assign xor_1_out = dividend ^ divisor;  // XOR_Gate xor_1, 4 bits wide
  assign controlled_buffer_1_out = dividend[3] ? xor_1_out : 4'bz;  // Controlled_Buffer controlled_buffer_2
  Bit_Extender #(.in_width(4), .out_width(3)) bit_extender_1 (.in(controlled_buffer_1_out), .out(remainder));
endmodule

module CRC (
  input  [7:0] A,
  input  [3:0] B,
  output [10:0] C
);

  wire [2:0] mod2div_2_remainder, mod2div_3_remainder, mod2div_4_remainder;
  wire [3:1] mod2div_1_remainder;

  mod2div mod2div_1 (.divisor(B), .dividend(A[7:4]), .remainder(mod2div_1_remainder));
  mod2div mod2div_2 (.divisor(B), .dividend({mod2div_1_remainder, A[3]}), .remainder(mod2div_2_remainder));
  mod2div mod2div_3 (.divisor(B), .dividend({mod2div_2_remainder, A[2]}), .remainder(mod2div_3_remainder));
  mod2div mod2div_4 (.divisor(B), .dividend({mod2div_3_remainder, A[1]}), .remainder(mod2div_4_remainder));
  mod2div mod2div_5 (.divisor(B), .dividend({mod2div_4_remainder, A[0]}), .remainder(C[2:0]));

  assign C[10:3] = A;

  // Other names for the same wires on the sheet: _0 = A[0]; _1 = A[1]; _2 = A[2]; _3 = A[3]; _4_7[3:0] = A[7:4];
  //   div[3:0] = B
endmodule
