// Logisim project P3.circ as structural Verilog: 7 circuits, main circuit main
module main (
  input  reset,
  output [31:0] Instruction,
  output RegWrite,
  output [4:0] RegAddr,
  output [31:0] RegWrite_2,
  output MemWrite,
  output [4:0] MemData,
  output [31:0] MemData_2
);

  wire ALUSrc, clock_1_out, div, jal, jr, lh, MemtoReg, mfhi, mflo, nPC_sel, RegDst, sh, Zero;
  wire [1:0] EXTop;
  wire [2:0] ALUctr;
  wire [4:0] multiplexer_1_out;
  wire [31:0] alu_1_result, divider_1_out, divider_1_rem, dm_1_data_out, immed32, multiplexer_3_out,
       multiplexer_4_out, multiplexer_5_out, multiplexer_6_out, PC, PC_4, reg1data, register_1_q,
       register_2_q;

  IFU ifu_1 (
    .immed26(Instruction[25:0]), .jal(jal), .jr(jr), .reg1data(reg1data), .immed32(immed32),
    .nPC_sel(nPC_sel), .Zero(Zero), .PC(PC), .Reset(reset), .PCnext(PC), .PC_4(PC_4),
    .Instruction(Instruction));
  Controller controller_1 (
    .op5(Instruction[31]), .op4(Instruction[30]), .op3(Instruction[29]), .op2(Instruction[28]),
    .op1(Instruction[27]), .op0(Instruction[26]), .func5(Instruction[5]), .func4(Instruction[4]),
    .func3(Instruction[3]), .func2(Instruction[2]), .func1(Instruction[1]), .func0(Instruction[0]),
    .RegDst(RegDst), .ALUSrc(ALUSrc), .MentoReg(MemtoReg), .RegWrite(RegWrite), .MemWrite(MemWrite),
    .nPC_sel(nPC_sel), .Extop1(EXTop[1]), .Extop0(EXTop[0]), .ALUctr2(ALUctr[2]), .ALUctr1(ALUctr[1]),
    .ALUctr0(ALUctr[0]), .jal(jal), .lh(lh), .jr(jr), .div(div), .mflo(mflo), .mfhi(mfhi), .sh(sh));
  Multiplexer #(.width(5)) multiplexer_1 (
    .in0(Instruction[20:16]), .in1(Instruction[15:11]), .out(multiplexer_1_out), .sel(RegDst));  // open: en
  EXT ext_1 (.immed16(Instruction[15:0]), .EXTop(EXTop), .immed32(immed32));
  Multiplexer #(.width(5)) multiplexer_2 (
    .in0(multiplexer_1_out), .in1({5{1'b1}}), .out(RegAddr), .sel(jal));  // open: en
  GRF grf_1 (
    .Write_data(RegWrite_2), .Read_reg1(Instruction[25:21]), .Read_reg2(Instruction[20:16]),
    .Write_reg(RegAddr), .Reset(reset), .RegWrite(RegWrite), .Read_data1(reg1data), .Read_data2(MemData_2));
  Multiplexer #(.width(32)) multiplexer_3 (
    .in0(MemData_2), .in1(immed32), .out(multiplexer_3_out), .sel(ALUSrc));  // open: en
  Divider #(.width(32)) divider_1 (
    .a(reg1data), .b(MemData_2), .out(divider_1_out), .rem(divider_1_rem));  // open: upper
  Clock clock_1 (.out(clock_1_out));
  ALU alu_1 (
    .A(reg1data), .B(multiplexer_3_out), .ALUOp(ALUctr), .Zero(Zero),
    .Result({alu_1_result[31:7], MemData, alu_1_result[1:0]}));
  Register #(.width(32)) register_1 (.D(divider_1_out), .en(div), .Q(register_1_q), .clk(clock_1_out), .clr(reset));
  Register #(.width(32)) register_2 (.D(divider_1_rem), .en(div), .Q(register_2_q), .clk(clock_1_out), .clr(reset));
  DM dm_1 (
    .addr1(alu_1_result[1]), .Address(MemData), .Data(MemData_2), .reset(reset), .sh(sh),
    .MemWrite(MemWrite), .lh(lh), .Data_out(dm_1_data_out));
  Multiplexer #(.width(32)) multiplexer_4 (
    .in0({alu_1_result[31:7], MemData, alu_1_result[1:0]}), .in1(dm_1_data_out), .out(multiplexer_4_out),
    .sel(MemtoReg));  // open: en
  Multiplexer #(.width(32)) multiplexer_5 (
    .in0(multiplexer_4_out), .in1(PC_4), .out(multiplexer_5_out), .sel(jal));  // open: en
  Multiplexer #(.width(32)) multiplexer_6 (
    .in0(multiplexer_5_out), .in1(register_1_q), .out(multiplexer_6_out), .sel(mflo));  // open: en
  Multiplexer #(.width(32)) multiplexer_7 (
    .in0(multiplexer_6_out), .in1(register_2_q), .out(RegWrite_2), .sel(mfhi));  // open: en

  // Other names for the same wires on the sheet: MemAddr[4:0] = MemData; Data[31:0] = RegWrite_2;
  //   immed16[15:0] = Instruction[15:0]; immed26[25:0] = Instruction[25:0]; rd[4:0] = Instruction[15:11];
  //   rt[4:0] = Instruction[20:16]; rs[4:0] = Instruction[25:21]; MemData_t[31:0] = MemData_2
endmodule

module EXT (
  input  [15:0] immed16,
  input  [1:0] EXTop,
  output [31:0] immed32
);

  wire [31:0] bit_extender_1_out, bit_extender_2_out, bit_extender_3_out, shifter_1_out;

  assign bit_extender_1_out = {{16{1'b0}}, immed16};  // Bit_Extender bit_extender_1
  assign bit_extender_2_out = {{16{immed16[15]}}, immed16};  // Bit_Extender bit_extender_2
  assign bit_extender_3_out = {{16{immed16[15]}}, immed16};  // Bit_Extender bit_extender_3
  Shifter #(.width(32)) shifter_1 (.in(bit_extender_3_out), .\dist (5'b00010), .out(shifter_1_out));
  Multiplexer #(.select(2), .width(32)) multiplexer_1 (
    .in0(bit_extender_1_out), .in1({immed16, {16{1'b0}}}), .in2(bit_extender_2_out), .in3(shifter_1_out),
    .out(immed32), .sel(EXTop));  // open: en
endmodule

module IFU (
  input  [25:0] immed26,
  input  jal,
  input  jr,
  input  [31:0] reg1data,
  input  [31:0] immed32,
  input  nPC_sel,
  input  Zero,
  input  [31:0] PC,
  input  Reset,
  output [31:0] PCnext,
  output [31:0] PC_4,
  output [31:0] Instruction
);

  wire and_1_out, clock_1_out, comparator_1_eq;
  wire [31:0] adder_2_out, multiplexer_1_out, multiplexer_2_out, multiplexer_3_out, PC_q, subtractor_1_out;

  Comparator #(.width(32), .mode("unsigned")) comparator_1 (
    .a({32{1'b0}}), .b(PC), .eq(comparator_1_eq));  // open: gt, lt
  Subtractor #(.width(32)) subtractor_1 (.a(PC), .b(32'h3000), .out(subtractor_1_out));  // open: bin, bout
  Multiplexer #(.width(32)) multiplexer_1 (
    .in0(subtractor_1_out), .in1(PC), .out(multiplexer_1_out), .sel(comparator_1_eq));  // open: en
  Register #(.width(32)) u_PC (.D(multiplexer_1_out), .Q(PC_q), .clk(clock_1_out), .clr(Reset));  // open: en
  Clock clock_1 (.out(clock_1_out));
  Adder #(.width(32)) adder_1 (.a(32'h3004), .b(PC_q), .out(PC_4));  // open: cin, cout
  Adder #(.width(32)) adder_2 (.a(PC_4), .b(immed32), .out(adder_2_out));  // open: cin, cout
  ROM #(.addrWidth(5), .dataWidth(32)) rom_1 (.addr(PC_q[6:2]), .data(Instruction));  // open: sel
  Multiplexer #(.width(32)) multiplexer_2 (
    .in0(PC_4), .in1(adder_2_out), .out(multiplexer_2_out), .sel(and_1_out));  // open: en
  and and_1 (and_1_out, nPC_sel, Zero);
  Multiplexer #(.width(32)) multiplexer_3 (
    .in0(multiplexer_2_out), .in1({PC_4[31:28], immed26, 2'b00}), .out(multiplexer_3_out), .sel(jal));  // open: en
  Multiplexer #(.width(32)) multiplexer_4 (
    .in0(multiplexer_3_out), .in1(reg1data), .out(PCnext), .sel(jr));  // open: en

  // Notes on the sheet:
  //   contents of rom_1 (hex, n*v repeats v):
  //   3404007b 348501c8 3c06007b 3c07ffff 868021 c48823 35080000 ad040000 ad050004 8d100000 8d110004
  //   34040001 34050002 34060001 10850003 0 10860002 0 34040000 34050000
endmodule

module GRF (
  input  Reset,
  input  [31:0] Write_data,
  input  [4:0] Read_reg1,
  input  [4:0] Read_reg2,
  input  [4:0] Write_reg,
  input  RegWrite,
  output [31:0] Read_data1,
  output [31:0] Read_data2
);

  wire and_1_out, and_2_out, and_3_out, and_4_out, and_5_out, and_6_out, and_7_out, and_8_out, and_9_out,
       and_10_out, and_11_out, and_12_out, and_13_out, and_14_out, and_15_out, and_16_out, and_17_out,
       and_18_out, and_19_out, and_20_out, and_21_out, and_22_out, and_23_out, and_24_out, and_25_out,
       and_26_out, and_27_out, and_28_out, and_29_out, and_30_out, and_31_out, and_32_out, clock_1_out,
       decoder_1_out0, decoder_1_out1, decoder_1_out2, decoder_1_out3, decoder_1_out4, decoder_1_out5,
       decoder_1_out6, decoder_1_out7, decoder_1_out8, decoder_1_out9, decoder_1_out10, decoder_1_out11,
       decoder_1_out12, decoder_1_out13, decoder_1_out14, decoder_1_out15, decoder_1_out16, decoder_1_out17,
       decoder_1_out18, decoder_1_out19, decoder_1_out20, decoder_1_out21, decoder_1_out22, decoder_1_out23,
       decoder_1_out24, decoder_1_out25, decoder_1_out26, decoder_1_out27, decoder_1_out28, decoder_1_out29,
       decoder_1_out30, decoder_1_out31;
  wire [31:0] Reg0, Reg1, Reg2, Reg3, Reg4, Reg5, Reg6, Reg7, Reg8, Reg9, Reg10, Reg11, Reg12, Reg13, Reg14,
       Reg15, Reg16, Reg17, Reg18, Reg19, Reg20, Reg21, Reg22, Reg23, Reg24, Reg25, Reg26, Reg27, Reg28,
       Reg29, Reg30, Reg31;

  Decoder #(.select(5)) decoder_1 (
    .out0(decoder_1_out0), .out1(decoder_1_out1), .out2(decoder_1_out2), .out3(decoder_1_out3),
    .out4(decoder_1_out4), .out5(decoder_1_out5), .out6(decoder_1_out6), .out7(decoder_1_out7),
    .out8(decoder_1_out8), .out9(decoder_1_out9), .out10(decoder_1_out10), .out11(decoder_1_out11),
    .out12(decoder_1_out12), .out13(decoder_1_out13), .out14(decoder_1_out14), .out15(decoder_1_out15),
    .out16(decoder_1_out16), .out17(decoder_1_out17), .out18(decoder_1_out18), .out19(decoder_1_out19),
    .out20(decoder_1_out20), .out21(decoder_1_out21), .out22(decoder_1_out22), .out23(decoder_1_out23),
    .out24(decoder_1_out24), .out25(decoder_1_out25), .out26(decoder_1_out26), .out27(decoder_1_out27),
    .out28(decoder_1_out28), .out29(decoder_1_out29), .out30(decoder_1_out30), .out31(decoder_1_out31),
    .sel(Write_reg));  // open: en
  Clock clock_1 (.out(clock_1_out));
  and and_1 (and_1_out, decoder_1_out0, RegWrite);
  and and_2 (and_2_out, decoder_1_out1, RegWrite);
  and and_3 (and_3_out, decoder_1_out2, RegWrite);
  and and_4 (and_4_out, decoder_1_out3, RegWrite);
  and and_5 (and_5_out, decoder_1_out4, RegWrite);
  and and_6 (and_6_out, decoder_1_out5, RegWrite);
  and and_7 (and_7_out, decoder_1_out6, RegWrite);
  and and_8 (and_8_out, decoder_1_out7, RegWrite);
  and and_9 (and_9_out, decoder_1_out8, RegWrite);
  and and_10 (and_10_out, decoder_1_out9, RegWrite);
  and and_11 (and_11_out, decoder_1_out10, RegWrite);
  and and_12 (and_12_out, decoder_1_out11, RegWrite);
  and and_13 (and_13_out, decoder_1_out12, RegWrite);
  and and_14 (and_14_out, decoder_1_out13, RegWrite);
  and and_15 (and_15_out, decoder_1_out14, RegWrite);
  and and_16 (and_16_out, decoder_1_out15, RegWrite);
  and and_17 (and_17_out, decoder_1_out16, RegWrite);
  and and_18 (and_18_out, decoder_1_out17, RegWrite);
  and and_19 (and_19_out, decoder_1_out18, RegWrite);
  and and_20 (and_20_out, decoder_1_out19, RegWrite);
  and and_21 (and_21_out, decoder_1_out20, RegWrite);
  and and_22 (and_22_out, decoder_1_out21, RegWrite);
  and and_23 (and_23_out, decoder_1_out22, RegWrite);
  and and_24 (and_24_out, decoder_1_out23, RegWrite);
  and and_25 (and_25_out, decoder_1_out24, RegWrite);
  and and_26 (and_26_out, decoder_1_out25, RegWrite);
  and and_27 (and_27_out, decoder_1_out26, RegWrite);
  and and_28 (and_28_out, decoder_1_out27, RegWrite);
  and and_29 (and_29_out, decoder_1_out28, RegWrite);
  and and_30 (and_30_out, decoder_1_out29, RegWrite);
  and and_31 (and_31_out, decoder_1_out30, RegWrite);
  and and_32 (and_32_out, decoder_1_out31, RegWrite);
  Register #(.width(32)) register_1 (.D({32{1'b0}}), .en(and_1_out), .Q(Reg0), .clk(clock_1_out), .clr(Reset));
  Register #(.width(32)) register_2 (.D(Write_data), .en(and_2_out), .Q(Reg1), .clk(clock_1_out), .clr(Reset));
  Register #(.width(32)) register_3 (.D(Write_data), .en(and_3_out), .Q(Reg2), .clk(clock_1_out), .clr(Reset));
  Register #(.width(32)) register_4 (.D(Write_data), .en(and_4_out), .Q(Reg3), .clk(clock_1_out), .clr(Reset));
  Register #(.width(32)) register_5 (.D(Write_data), .en(and_5_out), .Q(Reg4), .clk(clock_1_out), .clr(Reset));
  Register #(.width(32)) register_6 (.D(Write_data), .en(and_6_out), .Q(Reg5), .clk(clock_1_out), .clr(Reset));
  Register #(.width(32)) register_7 (.D(Write_data), .en(and_7_out), .Q(Reg6), .clk(clock_1_out), .clr(Reset));
  Register #(.width(32)) register_8 (.D(Write_data), .en(and_8_out), .Q(Reg7), .clk(clock_1_out), .clr(Reset));
  Register #(.width(32)) register_9 (.D(Write_data), .en(and_9_out), .Q(Reg8), .clk(clock_1_out), .clr(Reset));
  Register #(.width(32)) register_10 (.D(Write_data), .en(and_10_out), .Q(Reg9), .clk(clock_1_out), .clr(Reset));
  Register #(.width(32)) register_11 (.D(Write_data), .en(and_11_out), .Q(Reg10), .clk(clock_1_out), .clr(Reset));
  Register #(.width(32)) register_12 (.D(Write_data), .en(and_12_out), .Q(Reg11), .clk(clock_1_out), .clr(Reset));
  Register #(.width(32)) register_13 (.D(Write_data), .en(and_13_out), .Q(Reg12), .clk(clock_1_out), .clr(Reset));
  Register #(.width(32)) register_14 (.D(Write_data), .en(and_14_out), .Q(Reg13), .clk(clock_1_out), .clr(Reset));
  Register #(.width(32)) register_15 (.D(Write_data), .en(and_15_out), .Q(Reg14), .clk(clock_1_out), .clr(Reset));
  Register #(.width(32)) register_16 (.D(Write_data), .en(and_16_out), .Q(Reg15), .clk(clock_1_out), .clr(Reset));
  Register #(.width(32)) register_17 (.D(Write_data), .en(and_17_out), .Q(Reg16), .clk(clock_1_out), .clr(Reset));
  Register #(.width(32)) register_18 (.D(Write_data), .en(and_18_out), .Q(Reg17), .clk(clock_1_out), .clr(Reset));
  Register #(.width(32)) register_19 (.D(Write_data), .en(and_19_out), .Q(Reg18), .clk(clock_1_out), .clr(Reset));
  Register #(.width(32)) register_20 (.D(Write_data), .en(and_20_out), .Q(Reg19), .clk(clock_1_out), .clr(Reset));
  Register #(.width(32)) register_21 (.D(Write_data), .en(and_21_out), .Q(Reg20), .clk(clock_1_out), .clr(Reset));
  Register #(.width(32)) register_22 (.D(Write_data), .en(and_22_out), .Q(Reg21), .clk(clock_1_out), .clr(Reset));
  Register #(.width(32)) register_23 (.D(Write_data), .en(and_23_out), .Q(Reg22), .clk(clock_1_out), .clr(Reset));
  Register #(.width(32)) register_24 (.D(Write_data), .en(and_24_out), .Q(Reg23), .clk(clock_1_out), .clr(Reset));
  Register #(.width(32)) register_25 (.D(Write_data), .en(and_25_out), .Q(Reg24), .clk(clock_1_out), .clr(Reset));
  Register #(.width(32)) register_26 (.D(Write_data), .en(and_26_out), .Q(Reg25), .clk(clock_1_out), .clr(Reset));
  Register #(.width(32)) register_27 (.D(Write_data), .en(and_27_out), .Q(Reg26), .clk(clock_1_out), .clr(Reset));
  Register #(.width(32)) register_28 (.D(Write_data), .en(and_28_out), .Q(Reg27), .clk(clock_1_out), .clr(Reset));
  Register #(.width(32)) register_29 (.D(Write_data), .en(and_29_out), .Q(Reg28), .clk(clock_1_out), .clr(Reset));
  Register #(.width(32)) register_30 (.D(Write_data), .en(and_30_out), .Q(Reg29), .clk(clock_1_out), .clr(Reset));
  Register #(.width(32)) register_31 (.D(Write_data), .en(and_31_out), .Q(Reg30), .clk(clock_1_out), .clr(Reset));
  Register #(.width(32)) register_32 (.D(Write_data), .en(and_32_out), .Q(Reg31), .clk(clock_1_out), .clr(Reset));
  Multiplexer #(.select(5), .width(32)) multiplexer_1 (
    .in0(Reg0), .in1(Reg1), .in2(Reg2), .in3(Reg3), .in4(Reg4), .in5(Reg5), .in6(Reg6), .in7(Reg7),
    .in8(Reg8), .in9(Reg9), .in10(Reg10), .in11(Reg11), .in12(Reg12), .in13(Reg13), .in14(Reg14),
    .in15(Reg15), .in16(Reg16), .in17(Reg17), .in18(Reg18), .in19(Reg19), .in20(Reg20), .in21(Reg21),
    .in22(Reg22), .in23(Reg23), .in24(Reg24), .in25(Reg25), .in26(Reg26), .in27(Reg27), .in28(Reg28),
    .in29(Reg29), .in30(Reg30), .in31(Reg31), .out(Read_data1), .sel(Read_reg1));  // open: en
  Multiplexer #(.select(5), .width(32)) multiplexer_2 (
    .in0(Reg0), .in1(Reg1), .in2(Reg2), .in3(Reg3), .in4(Reg4), .in5(Reg5), .in6(Reg6), .in7(Reg7),
    .in8(Reg8), .in9(Reg9), .in10(Reg10), .in11(Reg11), .in12(Reg12), .in13(Reg13), .in14(Reg14),
    .in15(Reg15), .in16(Reg16), .in17(Reg17), .in18(Reg18), .in19(Reg19), .in20(Reg20), .in21(Reg21),
    .in22(Reg22), .in23(Reg23), .in24(Reg24), .in25(Reg25), .in26(Reg26), .in27(Reg27), .in28(Reg28),
    .in29(Reg29), .in30(Reg30), .in31(Reg31), .out(Read_data2), .sel(Read_reg2));  // open: en
endmodule

module DM (
  input  addr1,
  input  [4:0] Address,
  input  [31:0] Data,
  input  sh,
  input  lh,
  input  MemWrite,
  input  reset,
  output [31:0] Data_out
);

  wire clock_1_out;
  wire [15:0] multiplexer_1_out, multiplexer_3_out, ram_1_data, ram_1_data_2;
  wire [31:0] bit_extender_1_out, multiplexer_2_out;

  Multiplexer #(.width(16)) multiplexer_1 (
    .in0(ram_1_data_2), .in1(ram_1_data), .out(multiplexer_1_out), .sel(addr1));  // open: en
  Multiplexer #(.width(32)) multiplexer_2 (
    .in0(Data), .in1({multiplexer_1_out, Data[15:0]}), .out(multiplexer_2_out), .sel(sh));  // open: en
  Clock clock_1 (.out(clock_1_out));
  RAM #(.addrWidth(5), .dataWidth(32), .bus("separate")) ram_1 (
    .addr(Address), .din(multiplexer_2_out), .data({ram_1_data_2, ram_1_data}), .str(MemWrite),
    .clk(clock_1_out), .clr(reset));  // open: sel, ld
  Multiplexer #(.width(16)) multiplexer_3 (
    .in0(ram_1_data), .in1(ram_1_data_2), .out(multiplexer_3_out), .sel(addr1));  // open: en
  assign bit_extender_1_out = {{16{multiplexer_3_out[15]}}, multiplexer_3_out};  // Bit_Extender bit_extender_1
  Multiplexer #(.width(32)) multiplexer_4 (
    .in0({ram_1_data_2, ram_1_data}), .in1(bit_extender_1_out), .out(Data_out), .sel(lh));  // open: en
endmodule

module Controller (
  input  op5,
  input  op4,
  input  op3,
  input  op2,
  input  op1,
  input  op0,
  input  func5,
  input  func4,
  input  func3,
  input  func2,
  input  func1,
  input  func0,
  output RegDst,
  output ALUSrc,
  output MentoReg,
  output RegWrite,
  output MemWrite,
  output nPC_sel,
  output Extop1,
  output Extop0,
  output ALUctr2,
  output ALUctr1,
  output ALUctr0,
  output jal,
  output lh,
  output jr,
  output div,
  output mflo,
  output mfhi,
  output sh
);

  wire addu_out, lui_out, lw_out, nop_out, not_1_out, not_2_out, not_3_out, not_4_out, not_5_out, not_6_out,
       not_7_out, not_8_out, not_9_out, not_10_out, not_11_out, not_12_out, op_0, ori_out, subu_out, sw_out;

  not not_1 (not_1_out, op5);
  not not_2 (not_2_out, op4);
  not not_3 (not_3_out, func4);
  not not_4 (not_4_out, func5);
  not not_5 (not_5_out, op3);
  and and_1 (op_0, not_1_out, not_2_out, not_5_out, not_8_out, not_7_out, not_11_out);
  not not_6 (not_6_out, func3);
  not not_7 (not_7_out, op1);
  not not_8 (not_8_out, op2);
  not not_9 (not_9_out, func1);
  not not_10 (not_10_out, func2);
  not not_11 (not_11_out, op0);
  not not_12 (not_12_out, func0);
  and ori (ori_out, not_1_out, not_2_out, op3, op2, not_7_out, op0);
  and lw (lw_out, op5, not_2_out, not_5_out, not_8_out, op1, op0);
  and sw (sw_out, op5, not_2_out, op3, not_8_out, op1, op0);
  and beq (nPC_sel, not_1_out, not_2_out, not_5_out, op2, not_7_out, not_11_out);
  and lui (lui_out, not_1_out, not_2_out, op3, op2, op1, op0);
  and u_jal (jal, not_1_out, not_2_out, not_5_out, not_8_out, op1, op0);
  and xori (ALUctr2, not_1_out, not_2_out, op3, op2, op1, not_11_out);
  and u_lh (lh, op5, not_2_out, not_5_out, not_8_out, not_7_out, op0);
  and u_sh (sh, op5, not_2_out, op3, not_8_out, not_7_out, op0);
  and addu (addu_out, op_0, func5, not_3_out, not_6_out, not_10_out, not_9_out, func0);
  and subu (subu_out, func5, not_3_out, not_6_out, not_10_out, func1, func0, op_0);
  and nop (nop_out, not_4_out, not_3_out, not_6_out, not_10_out, not_9_out, not_12_out, op_0);
  and u_jr (jr, not_4_out, not_3_out, func3, not_10_out, not_9_out, not_12_out, op_0);
  and u_div (div, not_4_out, func4, func3, not_10_out, func1, not_12_out, op_0);
  and u_mflo (mflo, not_4_out, func4, not_6_out, not_10_out, func1, not_12_out, op_0);
  and u_mfhi (mfhi, not_4_out, func4, not_6_out, not_10_out, not_9_out, not_12_out, op_0);
  or u_RegDst (RegDst, addu_out, mfhi, mflo, subu_out);
  or u_ALUSrc (ALUSrc, lh, ori_out, lw_out, ALUctr2, sw_out, lui_out);
  or MemtoReg (MentoReg, lh, lw_out);
  or u_RegWrite (RegWrite, mflo, lh, addu_out, subu_out, jal, ALUctr2, ori_out, lw_out, lui_out, mfhi);
  or u_MemWrite (MemWrite, sw_out, sh);
  or u_Extop1 (Extop1, lw_out, sw_out, lh, nPC_sel);
  or u_Extop0 (Extop0, nPC_sel, lui_out);
  or u_ALUctr0 (ALUctr0, subu_out, lui_out);
  or u_ALUctr1 (ALUctr1, ori_out, lui_out);

  // Notes on the sheet:
  //   MemWrite
  //   nPC_sel
endmodule

module ALU (
  input  [31:0] A,
  input  [31:0] B,
  input  [2:0] ALUOp,
  output Zero,
  output [31:0] Result
);

  wire [31:0] adder_1_out, or_1_out, subtractor_1_out, xor_1_out;

  Comparator #(.width(32), .mode("unsigned")) comparator_1 (.a(A), .b(B), .eq(Zero));  // open: gt, lt
  Adder #(.width(32)) adder_1 (.a(A), .b(B), .out(adder_1_out));  // open: cin, cout
  Subtractor #(.width(32)) subtractor_1 (.a(A), .b(B), .out(subtractor_1_out));  // open: bin, bout
  assign or_1_out = A | B;  // OR_Gate or_1, 32 bits wide
  assign xor_1_out = A ^ B;  // XOR_Gate xor_1, 32 bits wide
  Multiplexer #(.select(3), .width(32)) multiplexer_1 (
    .in0(adder_1_out), .in1(subtractor_1_out), .in2(or_1_out), .in3(B), .in4(xor_1_out), .out(Result),
    .sel(ALUOp));  // open: in5, in6, in7, en
endmodule
