// Logisim project alu.circ as structural Verilog: 1 circuit, main circuit alu
module alu (
  input  [3:0] A,
  input  [3:0] B,
  input  [1:0] ALUOp,
  output [3:0] C
);

  wire _0, _1, _2, _3;
  wire [3:0] adder_1_out, and_1_out, or_1_out, subtractor_1_out;

  Decoder #(.select(2)) decoder_1 (.out0(_0), .out1(_1), .out2(_2), .out3(_3), .sel(ALUOp));  // open: en
  Adder #(.width(4)) adder_1 (.a(A), .b(B), .out(adder_1_out));  // open: cin, cout
  Subtractor #(.width(4)) subtractor_1 (.a(A), .b(B), .out(subtractor_1_out));  // open: bin, bout
  assign and_1_out = A & B;  // AND_Gate and_1, 4 bits wide
  assign or_1_out = A | B;  // OR_Gate or_1, 4 bits wide
  assign C = _0 ? adder_1_out : 4'bz;  // Controlled_Buffer controlled_buffer_1
  assign C = _1 ? subtractor_1_out : 4'bz;  // Controlled_Buffer controlled_buffer_2
  assign C = _2 ? and_1_out : 4'bz;  // Controlled_Buffer controlled_buffer_3
  assign C = _3 ? or_1_out : 4'bz;  // Controlled_Buffer controlled_buffer_4
endmodule
