// Logisim project challenge.circ as structural Verilog: 2 circuits, main circuit main
module main (
  input  [31:0] in_1,
  output [31:0] out_2
);

  wire bit_extender_1_out, clock_1_out, comparator_2_eq, controlled_buffer_1_out, first_flag, not_1_out,
       or_1_out;
  wire [31:0] _1, _2, _3, _4, _11, _12, _21, _22, counter_1_q, in, multiplexer_1_out, multiplexer_2_out,
       multiplexer_3_out, multiplexer_4_out, multiplexer_5_out, multiplexer_6_out, multiplexer_7_out,
       multiplexer_8_out, multiplexer_9_out, multiplexer_11_out, multiplexer_12_out, multiplexer_13_out,
       multiplexer_14_out, r11, r12, r21, r22, register_1_q, res_c_out11, res_c_out12, res_c_out21,
       res_c_out22, subtractor_1_out;

  assign controlled_buffer_1_out = not_1_out ? clock_1_out : 1'bz;  // Controlled_Buffer controlled_buffer_1
  Clock clock_1 (.out(clock_1_out));
  Counter #(.width(32), .max('hffffffff)) counter_1 (
    .Q(counter_1_q), .clk(controlled_buffer_1_out));  // open: load, D, count, carry, clr
  Subtractor #(.width(32)) subtractor_1 (.a(in_1), .b(32'h1), .out(subtractor_1_out));  // open: bin, bout
  Comparator #(.width(32), .mode("unsigned")) comparator_1 (
    .a({32{1'b0}}), .b(counter_1_q), .eq(first_flag));  // open: gt, lt
  Multiplexer #(.width(32)) multiplexer_1 (
    .in0(in), .in1(subtractor_1_out), .out(multiplexer_1_out), .sel(first_flag));  // open: en
  Register #(.width(32)) register_1 (
    .D(multiplexer_1_out), .Q(register_1_q), .clk(controlled_buffer_1_out));  // open: en, clr
  Comparator #(.width(32)) comparator_2 (.a(register_1_q), .b(32'h1), .eq(comparator_2_eq));  // open: gt, lt
  not not_1 (not_1_out, comparator_2_eq);
  Register #(.width(32)) register_2 (.D(multiplexer_2_out), .Q(_1), .clk(controlled_buffer_1_out));  // open: en, clr
  Multiplexer #(.width(32)) multiplexer_2 (
    .in0(_11), .in1(32'h1), .out(multiplexer_2_out), .sel(first_flag));  // open: en
  Multiplexer #(.width(32)) multiplexer_3 (
    .in0(_12), .in1(32'h1), .out(multiplexer_3_out), .sel(first_flag));  // open: en
  Register #(.width(32)) register_3 (.D(multiplexer_3_out), .Q(_2), .clk(controlled_buffer_1_out));  // open: en, clr
  Multiplexer #(.width(32)) multiplexer_4 (
    .in0(_21), .in1(32'h1), .out(multiplexer_4_out), .sel(first_flag));  // open: en
  Register #(.width(32)) register_4 (.D(multiplexer_4_out), .Q(_3), .clk(controlled_buffer_1_out));  // open: en, clr
  Multiplexer #(.width(32)) multiplexer_5 (
    .in0(_22), .in1({32{1'b0}}), .out(multiplexer_5_out), .sel(first_flag));  // open: en
  Register #(.width(32)) register_5 (.D(multiplexer_5_out), .Q(_4), .clk(controlled_buffer_1_out));  // open: en, clr
  Bit_Extender #(.in_width(32), .out_width(1)) bit_extender_1 (.in(register_1_q), .out(bit_extender_1_out));
  or or_1 (or_1_out, bit_extender_1_out, 1'b0);
  Divider #(.width(32)) divider_1 (.a(register_1_q), .b(32'h2), .out(in));  // open: upper, rem
  Multiplexer #(.width(32)) multiplexer_6 (.in0(32'h1), .in1(_1), .out(multiplexer_6_out), .sel(or_1_out));  // open: en
  Multiplexer #(.width(32)) multiplexer_7 (
    .in0({32{1'b0}}), .in1(_2), .out(multiplexer_7_out), .sel(or_1_out));  // open: en
  Multiplexer #(.width(32)) multiplexer_8 (
    .in0({32{1'b0}}), .in1(_2), .out(multiplexer_8_out), .sel(or_1_out));  // open: en
  Multiplexer #(.width(32)) multiplexer_9 (.in0(32'h1), .in1(_4), .out(multiplexer_9_out), .sel(or_1_out));  // open: en
  mult res_c (
    .c11(multiplexer_6_out), .c12(multiplexer_7_out), .c21(multiplexer_8_out), .c22(multiplexer_9_out),
    .res11(r11), .res12(r12), .res21(r21), .res22(r22), .out11(res_c_out11), .out12(res_c_out12),
    .out21(res_c_out21), .out22(res_c_out22));
  Multiplexer #(.width(32)) multiplexer_10 (
    .in0(res_c_out11), .in1({32{1'b0}}), .out(out_2), .sel(not_1_out));  // open: en
  mult c_c (
    .c11(_1), .c12(_2), .c21(_3), .c22(_4), .res11(_1), .res12(_2), .res21(_3), .res22(_4), .out11(_11),
    .out12(_12), .out21(_21), .out22(_22));
  Multiplexer #(.width(32)) multiplexer_11 (
    .in0(res_c_out11), .in1(32'h1), .out(multiplexer_11_out), .sel(first_flag));  // open: en
  Register #(.width(32)) register_6 (.D(multiplexer_11_out), .Q(r11), .clk(controlled_buffer_1_out));  // open: en, clr
  Register #(.width(32)) register_7 (.D(multiplexer_12_out), .Q(r12), .clk(controlled_buffer_1_out));  // open: en, clr
  Multiplexer #(.width(32)) multiplexer_12 (
    .in0(res_c_out12), .in1({32{1'b0}}), .out(multiplexer_12_out), .sel(first_flag));  // open: en
  Register #(.width(32)) register_8 (.D(multiplexer_13_out), .Q(r21), .clk(controlled_buffer_1_out));  // open: en, clr
  Multiplexer #(.width(32)) multiplexer_13 (
    .in0(res_c_out21), .in1({32{1'b0}}), .out(multiplexer_13_out), .sel(first_flag));  // open: en
  Register #(.width(32)) register_9 (.D(multiplexer_14_out), .Q(r22), .clk(controlled_buffer_1_out));  // open: en, clr
  Multiplexer #(.width(32)) multiplexer_14 (
    .in0(res_c_out22), .in1(32'h1), .out(multiplexer_14_out), .sel(first_flag));  // open: en
endmodule

module mult (
  input  [31:0] c11,
  input  [31:0] c12,
  input  [31:0] c21,
  input  [31:0] c22,
  input  [31:0] res11,
  input  [31:0] res12,
  input  [31:0] res21,
  input  [31:0] res22,
  output [31:0] out11,
  output [31:0] out12,
  output [31:0] out21,
  output [31:0] out22
);

  wire [31:0] multiplier_1_out, multiplier_2_out, multiplier_3_out, multiplier_4_out, multiplier_5_out,
       multiplier_6_out, multiplier_7_out, multiplier_8_out;

  Multiplier #(.width(32)) multiplier_1 (.a(c11), .b(res11), .out(multiplier_1_out));  // open: cin, cout
  Multiplier #(.width(32)) multiplier_2 (.a(c12), .b(res21), .out(multiplier_2_out));  // open: cin, cout
  Multiplier #(.width(32)) multiplier_3 (.a(c11), .b(res12), .out(multiplier_3_out));  // open: cin, cout
  Multiplier #(.width(32)) multiplier_4 (.a(c12), .b(res22), .out(multiplier_4_out));  // open: cin, cout
  Multiplier #(.width(32)) multiplier_5 (.a(c21), .b(res11), .out(multiplier_5_out));  // open: cin, cout
  Multiplier #(.width(32)) multiplier_6 (.a(c22), .b(res21), .out(multiplier_6_out));  // open: cin, cout
  Multiplier #(.width(32)) multiplier_7 (.a(c21), .b(res12), .out(multiplier_7_out));  // open: cin, cout
  Multiplier #(.width(32)) multiplier_8 (.a(c22), .b(res22), .out(multiplier_8_out));  // open: cin, cout
  Adder #(.width(32)) adder_1 (.a(multiplier_1_out), .b(multiplier_2_out), .out(out11));  // open: cin, cout
  Adder #(.width(32)) adder_2 (.a(multiplier_3_out), .b(multiplier_4_out), .out(out12));  // open: cin, cout
  Adder #(.width(32)) adder_3 (.a(multiplier_5_out), .b(multiplier_6_out), .out(out21));  // open: cin, cout
  Adder #(.width(32)) adder_4 (.a(multiplier_7_out), .b(multiplier_8_out), .out(out22));  // open: cin, cout
endmodule
