// Logisim project counter.circ as structural Verilog: 1 circuit, main circuit main
module main (
);

  wire clock_1_out;
  wire [7:0] counter_1_q, xor_1_out;

  Counter counter_1 (.Q(counter_1_q), .clk(clock_1_out));  // open: load, D, count, carry, clr
  assign xor_1_out = counter_1_q ^ 8'h34;  // XOR_Gate xor_1, 8 bits wide
  Clock clock_1 (.out(clock_1_out));
  RAM #(.bus("separate")) ram_1 (
    .addr(xor_1_out), .din(counter_1_q), .clk(clock_1_out));  // open: data, str, sel, ld, clr
endmodule
