// Logisim project fobi.circ as structural Verilog: 1 circuit, main circuit main
module main (
  input  [2:0] N,
  output [3:0] Nth
);

  wire clock_1_out, comparator_1_eq, controlled_buffer_1_out, not_1_out;
  wire [2:0] counter_1_q;
  wire [3:0] rom_1_data;

  Clock clock_1 (.out(clock_1_out));
  Counter #(.width(3), .max('h7)) counter_1 (
    .Q(counter_1_q), .clk(controlled_buffer_1_out));  // open: load, D, count, carry, clr
  assign controlled_buffer_1_out = not_1_out ? clock_1_out : 1'bz;  // Controlled_Buffer controlled_buffer_1
  ROM #(.addrWidth(3), .dataWidth(4)) rom_1 (.addr(counter_1_q), .data(rom_1_data));  // open: sel
  Comparator #(.width(3)) comparator_1 (.a(counter_1_q), .b(N), .eq(comparator_1_eq));  // open: gt, lt
  not not_1 (not_1_out, comparator_1_eq);
  Multiplexer #(.width(4)) multiplexer_1 (.in0(rom_1_data), .in1(4'b0000), .out(Nth), .sel(not_1_out));  // open: en

  // Notes on the sheet:
  //   contents of rom_1 (hex, n*v repeats v):
  //   0 1 1 2 3 5 8 d
endmodule
