// Logisim project fsm.circ as structural Verilog: 2 circuits, main circuit fsm
module fsmwork (
  input  In1,
  input  In0,
  input  statein_1,
  input  statein_0,
  output stateout_1,
  output stateout_0
);

  wire and_1_out, and_2_out, and_3_out, and_4_out, not_1_out, not_2_out, not_3_out, not_4_out, not_5_out,
       not_6_out, not_7_out;

  not not_1 (not_1_out, In0);
  not not_2 (not_2_out, statein_1);
  not not_3 (not_3_out, In0);
  not not_4 (not_4_out, statein_0);
  not not_5 (not_5_out, In0);
  not not_6 (not_6_out, statein_0);
  not not_7 (not_7_out, In1);
  and and_1 (and_1_out, not_1_out, not_2_out, statein_0);
  and and_2 (and_2_out, not_3_out, statein_1, not_4_out);
  and and_3 (and_3_out, not_5_out, statein_1, not_6_out);
  and and_4 (and_4_out, not_7_out, In0);
  or or_1 (stateout_1, and_1_out, and_2_out);
  or or_2 (stateout_0, and_3_out, and_4_out);
endmodule

module fsm (
  input  CLR,
  input  [1:0] In,
  output Z
);

  wire and_1_out, clock_1_out, comparator_1_eq, not_1_out, register_1_q, register_2_q, register_3_q;
  wire [1:0] fsmwork_1_stateout_0;

  Clock clock_1 (.out(clock_1_out));
  Register #(.width(1)) register_1 (
    .D(fsmwork_1_stateout_0[1]), .Q(register_1_q), .clk(clock_1_out), .clr(and_1_out));  // open: en
  Register #(.width(1)) register_2 (
    .D(fsmwork_1_stateout_0[0]), .Q(register_2_q), .clk(clock_1_out), .clr(and_1_out));  // open: en
  Register #(.width(1)) register_3 (.D(CLR), .Q(register_3_q), .clk(clock_1_out));  // open: en, clr
  fsmwork fsmwork_1 (
    .In1(In[1]), .In0(In[0]), .statein_1(register_1_q), .statein_0(register_2_q),
    .stateout_1(fsmwork_1_stateout_0[1]), .stateout_0(fsmwork_1_stateout_0[0]));
  and and_1 (and_1_out, register_3_q, CLR);
  // Probe on fsmwork_1_stateout_0
  Comparator #(.width(2), .mode("unsigned")) comparator_1 (
    .a(fsmwork_1_stateout_0), .b(2'b11), .eq(comparator_1_eq));  // open: gt, lt
  assign Z = comparator_1_eq ? 1'b1 : 1'bz;  // Controlled_Buffer controlled_buffer_1
  assign Z = not_1_out ? 1'b0 : 1'bz;  // Controlled_Buffer controlled_buffer_2
  not not_1 (not_1_out, comparator_1_eq);
endmodule
