// Logisim project mod.circ as structural Verilog: 2 circuits, main circuit output
module \output  (
  input  in,
  input  s2_in,
  input  s3_in,
  output s0_out,
  output s1_out,
  output s2_cycle,
  output s2_out,
  output s3_cycle,
  output s3_out,
  output s4_out
);

  wire and_3_out, and_4_out, and_5_out, and_6_out, clock_1_out, not_1_out, not_2_out, not_3_out, not_4_out,
       not_5_out, not_6_out, not_7_out;

  not not_1 (not_1_out, in);
  not not_2 (not_2_out, s2_in);
  not not_3 (not_3_out, s3_in);
  not not_4 (not_4_out, s2_in);
  not not_5 (not_5_out, s3_in);
  not not_6 (not_6_out, in);
  not not_7 (not_7_out, in);
  and and_1 (s1_out, not_1_out, not_2_out, not_3_out);
  and and_2 (s2_out, in, not_4_out, not_5_out);
  and and_3 (and_3_out, in, s3_in);
  or or_1 (s3_out, and_3_out, and_4_out);
  and and_4 (and_4_out, in, s2_in);
  and and_5 (and_5_out, not_6_out, s3_in);
  and and_6 (and_6_out, not_7_out, s2_in);
  or or_2 (s4_out, and_5_out, and_6_out);
  Register #(.width(1)) register_1 (.D(s2_out), .en(1'b1), .Q(s2_cycle), .clk(clock_1_out));  // open: clr
  Register #(.width(1)) register_2 (.D(s3_out), .en(1'b1), .Q(s3_cycle), .clk(clock_1_out));  // open: clr
  Clock clock_1 (.out(clock_1_out));

  assign s0_out = 1'b0;
endmodule

module mod5 (
  input  in,
  output S0,
  output S1,
  output S2,
  output S3,
  output S4
);

  wire output_1_s2_cycle, output_1_s3_cycle;

  \output  output_1 (
    .in(in), .s2_in(output_1_s2_cycle), .s3_in(output_1_s3_cycle), .s2_cycle(output_1_s2_cycle),
    .s3_cycle(output_1_s3_cycle), .s0_out(S0), .s1_out(S1), .s2_out(S2), .s3_out(S3), .s4_out(S4));
endmodule
