// Logisim project qiangda.circ as structural Verilog: 1 circuit, main circuit main
module main (
  input  A,
  input  B,
  input  J,
  input  C,
  output A_2,
  output B_2,
  output C_2
);

  wire clk, clock_1_out, clock_2_out, clock_3_out, nand_1_out, nand_2_out, nand_3_out, not_1_out, not_2_out,
       not_3_out;

  D_Flip_Flop d_ff_1 (.clk(clk), .D(A), .Q(A_2), .reset(J));  // open: Qn, preset, en
  D_Flip_Flop d_ff_2 (.clk(clk), .D(B), .Q(B_2), .reset(J));  // open: Qn, preset, en
  D_Flip_Flop d_ff_3 (.clk(clk), .D(C), .Q(C_2), .reset(J));  // open: Qn, preset, en
  not not_1 (not_1_out, A_2);
  Clock clock_1 (.out(clock_1_out));
  not not_2 (not_2_out, B_2);
  Clock clock_2 (.out(clock_2_out));
  not not_3 (not_3_out, C_2);
  Clock clock_3 (.out(clock_3_out));
  nand nand_1 (nand_1_out, not_1_out, clock_1_out);
  nand nand_2 (nand_2_out, not_2_out, clock_2_out);
  nand nand_3 (nand_3_out, not_3_out, clock_3_out);
  or or_1 (clk, nand_1_out, nand_2_out, nand_3_out);
endmodule
