// Logisim project swap.circ as structural Verilog: 1 circuit, main circuit swap
module swap (
  input  in_1,
  input  in_2,
  input  in_3,
  output O1,
  output O2
);

  wire not_1_out;

  assign {O1, O2} = in_3 ? {in_2, in_1} : 2'bz;  // Controlled_Buffer controlled_buffer_1
  assign {O2, O1} = not_1_out ? {in_2, in_1} : 2'bz;  // Controlled_Buffer controlled_buffer_2
  not not_1 (not_1_out, in_3);
endmodule
